# Fritzing sketch oving4 (saved by Fritzing 0.9.3b)
breadboards: 1

parts:
  Part1 = Arduino Uno (Rev3)
  Part2 = SRF05 Ultrasonic Rangefinder
  BT1 = Bluetooth HC-06u [package=THT]

nets:
  N1: Part1.D1/TX, BT1.RXD
  N2: Part1.D2, BT1.TXD
  N3: Part1.D5_PWM, Part2.Echo
  N4: Part1.D6_PWM, Part2.Trig
  VCC: Part1.5V, Part2.VCC, BT1.VCC
  GND: Part1.GND, Part2.GND, BT1.GND

custom parts:
  Bluetooth HC-06u: Bluetooth HC-06 - face up, pins down 16.5mm x 37.5mm PCB
